// Logisim project Circuito com Memoria 256 bytes.circ as structural Verilog: 12 circuits, main circuit main
module main (
  input  in_1,
  input  [7:0] in_2,
  input  in_3,
  input  in_4,
  input  in_5,
  input  in_6,
  input  in_7,
  input  in_8,
  input  in_9,
  input  in_10,
  input  [1:0] in_11
);

  wire decoder_1_out0, decoder_1_out1, decoder_1_out2, decoder_1_out3, or_1_out;
  wire [7:0] controlled_buffer_1_out, register_1_q;

  assign controlled_buffer_1_out = in_3 ? in_2 : 8'bz;  // Controlled_Buffer controlled_buffer_1
  Decoder #(.disabled("Z"), .select(2)) decoder_1 (
    .out0(decoder_1_out0), .out1(decoder_1_out1), .out2(decoder_1_out2), .out3(decoder_1_out3), .sel(in_11),
    .en(in_10));
  memoria1byteSetEnable memoria1bytesetenable_1 (
    .in_1(controlled_buffer_1_out), .in_2(in_4), .in_3(decoder_1_out0), .out_4(controlled_buffer_1_out));
  memoria1byteSetEnable memoria1bytesetenable_2 (
    .in_1(controlled_buffer_1_out), .in_2(in_5), .in_3(decoder_1_out1), .out_4(controlled_buffer_1_out));
  memoria1byteSetEnable memoria1bytesetenable_3 (
    .in_1(controlled_buffer_1_out), .in_2(in_6), .in_3(decoder_1_out2), .out_4(controlled_buffer_1_out));
  memoria1byteSetEnable memoria1bytesetenable_4 (
    .in_1(controlled_buffer_1_out), .in_2(in_7), .in_3(decoder_1_out3), .out_4(controlled_buffer_1_out));
  RAM #(.databus("bidir")) ram_1 (.addr(register_1_q), .we(in_8), .oe(in_9), .clk(or_1_out));  // open: data
  Register register_1 (.D(controlled_buffer_1_out), .Q(register_1_q), .clk(in_1));  // open: en, clr
  or or_1 (or_1_out, in_9, in_8);
  // Probe on controlled_buffer_1_out

  // Notes on the sheet:
  //   Natasha Araujo Caxias N 22401912
  //   Barramento com 4 registradores + MAR + memoria 256 bytes
endmodule

module somador1bit (
  input  c_in,
  input  a,
  input  b,
  output saida,
  output c_out
);

  wire and_1_out, and_2_out, and_3_out, xor_1_out;

  xor xor_1 (xor_1_out, a, b);
  and and_1 (and_1_out, a, c_in);
  and and_2 (and_2_out, a, b);
  and and_3 (and_3_out, b, c_in);
  xor xor_2 (saida, xor_1_out, c_in);
  or or_1 (c_out, and_1_out, and_2_out, and_3_out);
endmodule

module somador8bits (
  input  c_in,
  input  [7:0] a,
  input  [7:0] b,
  output [7:0] saida,
  output c_out
);

  wire somador1bit_1_c_out, somador1bit_2_c_out, somador1bit_3_c_out, somador1bit_4_c_out,
       somador1bit_5_c_out, somador1bit_6_c_out, somador1bit_7_c_out;

  somador1bit somador1bit_1 (.a(a[0]), .b(b[0]), .c_in(c_in), .c_out(somador1bit_1_c_out), .saida(saida[0]));
  somador1bit somador1bit_2 (
    .a(a[1]), .b(b[1]), .c_in(somador1bit_1_c_out), .c_out(somador1bit_2_c_out), .saida(saida[1]));
  somador1bit somador1bit_3 (
    .a(a[2]), .b(b[2]), .c_in(somador1bit_2_c_out), .c_out(somador1bit_3_c_out), .saida(saida[2]));
  somador1bit somador1bit_4 (
    .a(a[3]), .b(b[3]), .c_in(somador1bit_3_c_out), .c_out(somador1bit_4_c_out), .saida(saida[3]));
  somador1bit somador1bit_5 (
    .a(a[4]), .b(b[4]), .c_in(somador1bit_4_c_out), .c_out(somador1bit_5_c_out), .saida(saida[4]));
  somador1bit somador1bit_6 (
    .a(a[5]), .b(b[5]), .c_in(somador1bit_5_c_out), .c_out(somador1bit_6_c_out), .saida(saida[5]));
  somador1bit somador1bit_7 (
    .a(a[6]), .b(b[6]), .c_in(somador1bit_6_c_out), .c_out(somador1bit_7_c_out), .saida(saida[6]));
  somador1bit somador1bit_8 (.a(a[7]), .b(b[7]), .c_in(somador1bit_7_c_out), .c_out(c_out), .saida(saida[7]));
endmodule

module memoria1bit (
  input  entrada,
  input  set,
  output saida
);

  wire nand_1_out, nand_2_out, nand_4_out;

  nand nand_1 (nand_1_out, entrada, set);
  nand nand_2 (nand_2_out, nand_1_out, set);
  nand nand_3 (saida, nand_1_out, nand_4_out);
  nand nand_4 (nand_4_out, saida, nand_2_out);
endmodule

module memoria1byteSet (
  input  in_1,
  input  in_2,
  input  in_3,
  input  in_4,
  input  in_5,
  input  in_6,
  input  in_7,
  input  in_8,
  input  in_9,
  output out_10,
  output out_11,
  output out_12,
  output out_13,
  output out_14,
  output out_15,
  output out_16,
  output out_17
);

  memoria1bit memoria1bit_1 (.entrada(in_1), .set(in_9), .saida(out_10));
  memoria1bit memoria1bit_2 (.entrada(in_2), .set(in_9), .saida(out_11));
  memoria1bit memoria1bit_3 (.entrada(in_3), .set(in_9), .saida(out_12));
  memoria1bit memoria1bit_4 (.entrada(in_4), .set(in_9), .saida(out_13));
  memoria1bit memoria1bit_5 (.entrada(in_5), .set(in_9), .saida(out_14));
  memoria1bit memoria1bit_6 (.entrada(in_6), .set(in_9), .saida(out_15));
  memoria1bit memoria1bit_7 (.entrada(in_7), .set(in_9), .saida(out_16));
  memoria1bit memoria1bit_8 (.entrada(in_8), .set(in_9), .saida(out_17));
endmodule

module memoria1byteSetEnable (
  input  [7:0] in_1,
  input  in_2,
  input  in_3,
  output [7:0] out_4
);

  wire memoria1byteset_1_out_10, memoria1byteset_1_out_11, memoria1byteset_1_out_12,
       memoria1byteset_1_out_13, memoria1byteset_1_out_14, memoria1byteset_1_out_15,
       memoria1byteset_1_out_16, memoria1byteset_1_out_17;
  wire [7:0] enable_1_out_10;

  memoria1byteSet memoria1byteset_1 (
    .in_1(in_1[0]), .in_2(in_1[1]), .in_3(in_1[2]), .in_4(in_1[3]), .in_5(in_1[4]), .in_6(in_1[5]),
    .in_7(in_1[6]), .in_8(in_1[7]), .in_9(in_2), .out_10(memoria1byteset_1_out_10),
    .out_11(memoria1byteset_1_out_11), .out_12(memoria1byteset_1_out_12), .out_13(memoria1byteset_1_out_13),
    .out_14(memoria1byteset_1_out_14), .out_15(memoria1byteset_1_out_15), .out_16(memoria1byteset_1_out_16),
    .out_17(memoria1byteset_1_out_17));
  enable enable_1 (
    .in_1(memoria1byteset_1_out_10), .in_2(memoria1byteset_1_out_11), .in_3(memoria1byteset_1_out_12),
    .in_4(memoria1byteset_1_out_13), .in_5(memoria1byteset_1_out_14), .in_6(memoria1byteset_1_out_15),
    .in_7(memoria1byteset_1_out_16), .in_8(memoria1byteset_1_out_17), .in_9(in_3),
    .out_10(enable_1_out_10[0]), .out_11(enable_1_out_10[1]), .out_12(enable_1_out_10[2]),
    .out_13(enable_1_out_10[3]), .out_14(enable_1_out_10[4]), .out_15(enable_1_out_10[5]),
    .out_16(enable_1_out_10[6]), .out_17(enable_1_out_10[7]));
  assign out_4 = in_3 ? enable_1_out_10 : 8'bz;  // Controlled_Buffer controlled_buffer_1
endmodule

module enable (
  input  in_1,
  input  in_2,
  input  in_3,
  input  in_4,
  input  in_5,
  input  in_6,
  input  in_7,
  input  in_8,
  input  in_9,
  output out_10,
  output out_11,
  output out_12,
  output out_13,
  output out_14,
  output out_15,
  output out_16,
  output out_17
);

  and and_1 (out_10, in_1, in_9);
  and and_2 (out_11, in_2, in_9);
  and and_3 (out_12, in_3, in_9);
  and and_4 (out_13, in_4, in_9);
  and and_5 (out_14, in_5, in_9);
  and and_6 (out_15, in_6, in_9);
  and and_7 (out_16, in_7, in_9);
  and and_8 (out_17, in_8, in_9);
endmodule

module decoder2x4 (
  input  in_1,
  input  in_2,
  output out_3,
  output out_4,
  output out_5,
  output out_6
);

  wire not_1_out, not_2_out;

  not not_1 (not_1_out, in_2);
  not not_2 (not_2_out, in_1);
  and and_1 (out_3, not_2_out, not_1_out);
  and and_2 (out_4, not_2_out, in_2);
  and and_3 (out_5, in_1, not_1_out);
  and and_4 (out_6, in_1, in_2);
endmodule

module memory256 (
  input  [7:0] in_1,
  input  we,
  input  oe,
  input  [7:0] in_4,
  output [7:0] out_5
);

  wire and_1_out, and_2_out, and_3_out, decoder_1_out0, decoder_2_out0;

  Decoder #(.enable("false"), .select(4)) decoder_1 (
    .out0(decoder_1_out0), .sel(in_1[7:4]));  // open: out1, out2, out3, out4, out5, out6, out7, out8, out9, out10, out11, out12, out13, out14, out15
  Decoder #(.enable("false"), .select(4)) decoder_2 (
    .out0(decoder_2_out0), .sel(in_1[3:0]));  // open: out1, out2, out3, out4, out5, out6, out7, out8, out9, out10, out11, out12, out13, out14, out15
  and and_1 (and_1_out, decoder_2_out0, decoder_1_out0);
  and and_2 (and_2_out, and_1_out, we);
  and and_3 (and_3_out, and_1_out, oe);
  memoria1byteSetEnable memoria1bytesetenable_1 (.in_1(in_4), .in_2(and_2_out), .in_3(and_3_out), .out_4(out_5));
endmodule

module SHR (
  input  in_1,
  input  [7:0] in_2,
  output [7:0] out_3,
  output out_4
);


  assign in_2[0] = in_1;
  assign out_3[6:0] = in_2[7:1];
  assign out_4 = out_3[7];
endmodule

module ULA (
  input  [7:0] in_1,
  input  [7:0] in_2,
  input  in_3,
  input  in_4,
  input  in_5,
  output [7:0] out_6,
  output out_7,
  output [7:0] out_8,
  output out_9,
  output [7:0] out_10,
  output out_11
);

  Adder adder_1 (.a(in_1), .b(in_2), .out(out_6), .cin(in_3), .cout(out_7));
  SHR shr_1 (.in_2(in_1), .in_1(in_4), .out_4(out_9), .out_3(out_8));
  SHL shl_1 (.in_1(in_1), .out_3(in_5), .in_2(out_11), .out_4(out_10));
endmodule

module SHL (
  input  [7:0] in_1,
  input  in_2,
  output out_3,
  output [7:0] out_4
);


  assign out_3 = in_1[0];
  assign out_4 = {in_2, in_1[7:1]};
endmodule
